# Fritzing sketch dooropener3 (saved by Fritzing 0.9.2b)
circuit board: 5.9439cm x 4.64039cm

parts:
  S1 = Toggle Switch [package=THT]
  J1 = Screw terminal - 2 pins [package=THT]
  C1 = Electrolytic Capacitor [capacitance=10µF package="100 mil [THT, electrolytic]"]
  C2 = Electrolytic Capacitor [capacitance=10µF package="100 mil [THT, electrolytic]"]
  LED1 = LED - 3mm [color="Red (633nm)" package="3 mm [THT]"]
  R1 = Resistor [tolerance=±5% resistance=330 package="2010 [SMD]"]
  XTAL1 = CRYSTAL - kHz [frequency="16 MHz"]
  C3 = Ceramic Capacitor [capacitance=22pF package="100 mil [THT, multilayer]"]
  C4 = Ceramic Capacitor [capacitance=22pF package="100 mil [THT, multilayer]"]
  R2 = Resistor [tolerance=±5% resistance=10k package=THT]
  C5 = Electrolytic Capacitor [capacitance=10µF package="100 mil [THT, electrolytic]"]
  IC1 = Voltage Regulator [package=to220-igo]
  MD09B1 = A4988 Stepper Motor Driver Carrier
  J2 = Screw terminal - 2 pins [package=THT]
  J3 = Screw terminal - 2 pins [package=THT]
  J4 = Screw terminal - 2 pins [package=THT]
  C6 = Electrolytic Capacitor [capacitance=1µF package="100 mil [THT, electrolytic]"]
  U2 = Voltage Regulator - 3.3V [package="TO220 [THT]"]
  RC522 = RFID-RC522-v2
  U1 = atmega168 [package=dip]
  C7 = Electrolytic Capacitor [capacitance=10µF package="100 mil [THT, electrolytic]"]
  JP1 = Header 3 [package=jst-3-pth]

nets:
  GND: S1.L1, J1.pin1, C1.-, C2.-, LED1.cathode, C3.1, C4.0, IC1.GND, MD09B1.GROUND#147, U2.GND, RC522.GND, U1.GND, C7.-
  N1: S1.COM, C5.+, U1.RESET
  N2: S1.L2, R2.Pin_0
  N3: J1.pin2, C1.+, IC1.IN, U2.input_voltage
  VDD: C2.+, R1.Pin_0, R2.Pin_1, IC1.OUT, MD09B1.VDD, U1.VCC, U1.AVCC, U1.AREF
  N4: LED1.anode, R1.Pin_1
  N5: XTAL1.pin_0, C3.0, U1.XLAT1
  N6: XTAL1.pin_1, C4.1, U1.XLAT2
  N7: C5.-, JP1.1
  N8: MD09B1.Enable, U1.D2
  N9: MD09B1.RESET, MD09B1.SLEEP
  N10: MD09B1.STEP, U1.D3_(PWM)
  N11: MD09B1.DIR, U1.D4
  N12: MD09B1.VMOT, J2.pin1, C6.+
  N13: MD09B1.GROUND#141, J2.pin2, C6.-
  N14: MD09B1.OUT_2B, J3.pin1
  N15: MD09B1.OUT_2A, J3.pin2
  N16: MD09B1.OUT_1A, J4.pin1
  N17: MD09B1.OUT_1B, J4.pin2
  N18: U2.output_voltage, RC522.3_3V, C7.+
  N19: RC522.SDA, U1.D10_(PWM)
  N20: RC522.SCK, U1.D13
  N21: RC522.MOSI, U1.D11_(PWM)
  N22: RC522.MISO, U1.D12
  N23: RC522.RST, U1.D9_(PWM)
  N24: U1.D0_(RX), JP1.2
  N25: U1.D1_(TX), JP1.3

custom parts:
  RFID-RC522-v2: A simple China made RFID-RC522 Reader; do check the pin labels, as this is a MFRC522 based clone.
